# Fritzing sketch petmoj (saved by Fritzing 0.9.2b)
circuit board: 8.46667cm x 5.64444cm

parts:
  Arduino_Uno = Arduino Uno (Rev3)
  Rotary_Dial = mystery part, 3 pins [chip_label=?]

nets:
  N1: Arduino_Uno.GND, Rotary_Dial.pin1
  N2: Arduino_Uno.D2, Rotary_Dial.pin2
  N3: Arduino_Uno.D4, Rotary_Dial.pin3
